// Logisim project banco_de_registradores.circ as structural Verilog: 2 circuits, main circuit main
module main (
  input  [3:0] RD,
  input  [3:0] Resultado,
  input  in_3,
  input  [3:0] RG1,
  input  [3:0] RG2,
  output [3:0] ULA_A,
  output [3:0] ULA_B
);

  wire clock_1_out, decoder_1_out0, decoder_1_out1, decoder_1_out2, decoder_1_out3, decoder_1_out4,
       decoder_1_out5, decoder_1_out6, decoder_1_out7, decoder_1_out8, decoder_1_out9, decoder_1_out10,
       decoder_1_out11, decoder_1_out12, decoder_1_out13, decoder_1_out14, decoder_1_out15;
  wire [3:0] registradores_1_r0, registradores_1_r1, registradores_1_r2, registradores_1_r3,
       registradores_1_r4, registradores_1_r5, registradores_1_r6, registradores_1_r7, registradores_1_r8,
       registradores_1_r9, registradores_1_r10, registradores_1_r11, registradores_1_r12,
       registradores_1_r13, registradores_1_r14, registradores_1_r15;

  Decoder #(.select(4)) decoder_1 (
    .out0(decoder_1_out0), .out1(decoder_1_out1), .out2(decoder_1_out2), .out3(decoder_1_out3),
    .out4(decoder_1_out4), .out5(decoder_1_out5), .out6(decoder_1_out6), .out7(decoder_1_out7),
    .out8(decoder_1_out8), .out9(decoder_1_out9), .out10(decoder_1_out10), .out11(decoder_1_out11),
    .out12(decoder_1_out12), .out13(decoder_1_out13), .out14(decoder_1_out14), .out15(decoder_1_out15),
    .sel(RD));  // open: en
  Clock clock_1 (.out(clock_1_out));
  registradores registradores_1 (
    .Resultado(Resultado), .en1(decoder_1_out0), .en2(decoder_1_out1), .en3(decoder_1_out2),
    .en4(decoder_1_out3), .e5(decoder_1_out4), .en6(decoder_1_out5), .en7(decoder_1_out6),
    .en8(decoder_1_out7), .en9(decoder_1_out8), .en10(decoder_1_out9), .en11(decoder_1_out10),
    .en12(decoder_1_out11), .en13(decoder_1_out12), .en14(decoder_1_out13), .en15(decoder_1_out14),
    .en16(decoder_1_out15), .WriteEnable(in_3), .clk(clock_1_out), .R0(registradores_1_r0),
    .R1(registradores_1_r1), .R2(registradores_1_r2), .R3(registradores_1_r3), .R4(registradores_1_r4),
    .R5(registradores_1_r5), .R6(registradores_1_r6), .R7(registradores_1_r7), .R8(registradores_1_r8),
    .R9(registradores_1_r9), .R10(registradores_1_r10), .R11(registradores_1_r11), .R12(registradores_1_r12),
    .R13(registradores_1_r13), .R14(registradores_1_r14), .R15(registradores_1_r15));
  Multiplexer #(.select(4), .width(4)) multiplexer_1 (
    .in0(registradores_1_r0), .in1(registradores_1_r1), .in2(registradores_1_r2), .in3(registradores_1_r3),
    .in4(registradores_1_r4), .in5(registradores_1_r5), .in6(registradores_1_r6), .in7(registradores_1_r7),
    .in8(registradores_1_r8), .in9(registradores_1_r9), .in10(registradores_1_r10),
    .in11(registradores_1_r11), .in12(registradores_1_r12), .in13(registradores_1_r13),
    .in14(registradores_1_r14), .in15(registradores_1_r15), .out(ULA_A), .sel(RG1));  // open: en
  Multiplexer #(.select(4), .width(4)) multiplexer_2 (
    .in0(registradores_1_r0), .in1(registradores_1_r1), .in2(registradores_1_r2), .in3(registradores_1_r3),
    .in4(registradores_1_r4), .in5(registradores_1_r5), .in6(registradores_1_r6), .in7(registradores_1_r7),
    .in8(registradores_1_r8), .in9(registradores_1_r9), .in10(registradores_1_r10),
    .in11(registradores_1_r11), .in12(registradores_1_r12), .in13(registradores_1_r13),
    .in14(registradores_1_r14), .in15(registradores_1_r15), .out(ULA_B), .sel(RG2));  // open: en
endmodule

module registradores (
  input  [3:0] Resultado,
  input  en1,
  input  en2,
  input  en3,
  input  en4,
  input  e5,
  input  en6,
  input  en7,
  input  en8,
  input  en9,
  input  en10,
  input  en11,
  input  en12,
  input  en13,
  input  en14,
  input  en15,
  input  en16,
  input  WriteEnable,
  input  clk,
  output [3:0] R0,
  output [3:0] R1,
  output [3:0] R2,
  output [3:0] R3,
  output [3:0] R4,
  output [3:0] R5,
  output [3:0] R6,
  output [3:0] R7,
  output [3:0] R8,
  output [3:0] R9,
  output [3:0] R10,
  output [3:0] R11,
  output [3:0] R12,
  output [3:0] R13,
  output [3:0] R14,
  output [3:0] R15
);

  wire and_1_out, and_2_out, and_3_out, and_4_out, and_5_out, and_6_out, and_7_out, and_8_out, and_9_out,
       and_10_out, and_11_out, and_12_out, and_13_out, and_14_out, and_15_out, and_16_out;

  and and_1 (and_1_out, en1, WriteEnable);
  and and_2 (and_2_out, en2, WriteEnable);
  and and_3 (and_3_out, en3, WriteEnable);
  and and_4 (and_4_out, en4, WriteEnable);
  and and_5 (and_5_out, e5, WriteEnable);
  and and_6 (and_6_out, en6, WriteEnable);
  and and_7 (and_7_out, en7, WriteEnable);
  and and_8 (and_8_out, en8, WriteEnable);
  and and_9 (and_9_out, en9, WriteEnable);
  and and_10 (and_10_out, en10, WriteEnable);
  and and_11 (and_11_out, en11, WriteEnable);
  and and_12 (and_12_out, en12, WriteEnable);
  and and_13 (and_13_out, en13, WriteEnable);
  and and_14 (and_14_out, en14, WriteEnable);
  and and_15 (and_15_out, en15, WriteEnable);
  and and_16 (and_16_out, en16, WriteEnable);
  Register #(.width(4)) u_R0 (.D(Resultado), .en(and_1_out), .Q(R0), .clk(clk));  // open: clr
  Register #(.width(4)) u_R1 (.D(Resultado), .en(and_2_out), .Q(R1), .clk(clk));  // open: clr
  Register #(.width(4)) u_R2 (.D(Resultado), .en(and_3_out), .Q(R2), .clk(clk));  // open: clr
  Register #(.width(4)) u_R3 (.D(Resultado), .en(and_4_out), .Q(R3), .clk(clk));  // open: clr
  Register #(.width(4)) u_R4 (.D(Resultado), .en(and_5_out), .Q(R4), .clk(clk));  // open: clr
  Register #(.width(4)) u_R5 (.D(Resultado), .en(and_6_out), .Q(R5), .clk(clk));  // open: clr
  Register #(.width(4)) u_R6 (.D(Resultado), .en(and_7_out), .Q(R6), .clk(clk));  // open: clr
  Register #(.width(4)) u_R7 (.D(Resultado), .en(and_8_out), .Q(R7), .clk(clk));  // open: clr
  Register #(.width(4)) u_R8 (.D(Resultado), .en(and_9_out), .Q(R8), .clk(clk));  // open: clr
  Register #(.width(4)) u_R9 (.D(Resultado), .en(and_10_out), .Q(R9), .clk(clk));  // open: clr
  Register #(.width(4)) u_R10 (.D(Resultado), .en(and_11_out), .Q(R10), .clk(clk));  // open: clr
  Register #(.width(4)) u_R11 (.D(Resultado), .en(and_12_out), .Q(R11), .clk(clk));  // open: clr
  Register #(.width(4)) u_R12 (.D(Resultado), .en(and_13_out), .Q(R12), .clk(clk));  // open: clr
  Register #(.width(4)) u_R13 (.D(Resultado), .en(and_14_out), .Q(R13), .clk(clk));  // open: clr
  Register #(.width(4)) u_R14 (.D(Resultado), .en(and_15_out), .Q(R14), .clk(clk));  // open: clr
  Register #(.width(4)) u_R15 (.D(Resultado), .en(and_16_out), .Q(R15), .clk(clk));  // open: clr
endmodule
